// Logisim project add2_j.circ as structural Verilog: 7 circuits, main circuit main
module main (
  input  in_1,
  output [31:0] out_2,
  output out_3,
  output [4:0] out_4,
  output [31:0] out_5,
  output out_6,
  output [4:0] out_7,
  output [31:0] out_8
);

  wire clk, controller_1_alubsel, controller_1_dm_re, controller_1_pcsel, controller_1_signextsel;
  wire [1:0] alu_1_compare, controller_1_dmoutsel, controller_1_grf_a3sel, controller_1_grf_wdsel;
  wire [2:0] controller_1_alu_op, controller_1_basel;
  wire [31:0] alu_1_out_4, badder_1_out_6, bit_extender_1_out, bit_extender_2_out, dm_1_out_8, grf_1_out_8,
       ifu_1_out_6, multiplexer_2_out, multiplexer_3_out;

  Clock clock_1 (.out(clk));
  IFU ifu_1 (
    .in_1(clk), .in_2(in_1), .in_3(controller_1_pcsel), .in_4(badder_1_out_6), .out_5(out_2),
    .out_6(ifu_1_out_6));
  Controller controller_1 (
    .op(out_2[31:26]), .func(out_2[5:0]), .PCsel(controller_1_pcsel), .GRF_WE(out_3),
    .ALU_OP(controller_1_alu_op), .DM_WE(out_6), .DM_RE(controller_1_dm_re),
    .GRF_A3sel(controller_1_grf_a3sel), .ALUBsel(controller_1_alubsel), .GRF_WDsel(controller_1_grf_wdsel),
    .signextsel(controller_1_signextsel), .DMoutsel(controller_1_dmoutsel), .Basel(controller_1_basel));
  Badder badder_1 (
    .ad1(controller_1_basel), .in_2(ifu_1_out_6), .in_3(multiplexer_2_out), .compare(alu_1_compare),
    .in_5(out_2), .out_6(badder_1_out_6));
  Multiplexer #(.select(2), .width(5)) multiplexer_1 (
    .in0(out_2[20:16]), .in1(out_2[15:11]), .out(out_4), .sel(controller_1_grf_a3sel));  // open: in2, in3, en
  assign bit_extender_1_out = {{16{out_2[15]}}, out_2[15:0]};  // Bit_Extender bit_extender_1
  assign bit_extender_2_out = {{16{1'b0}}, out_2[15:0]};  // Bit_Extender bit_extender_2
  GRF grf_1 (
    .WE(out_3), .reset(in_1), .clk(clk), .A(out_2[25:21]), .A2(out_2[20:16]), .A3(out_4), .in_7(out_5),
    .out_8(grf_1_out_8), .out_9(out_8));
  Multiplexer #(.width(32)) multiplexer_2 (
    .in0(bit_extender_1_out), .in1(bit_extender_2_out), .out(multiplexer_2_out), .sel(controller_1_signextsel));  // open: en
  ALU alu_1 (
    .in_1(grf_1_out_8), .in_2(multiplexer_3_out), .in_3(controller_1_alu_op),
    .out_4({alu_1_out_4[31:7], out_7, alu_1_out_4[1:0]}), .compare(alu_1_compare));
  Multiplexer #(.width(32)) multiplexer_3 (
    .in0(out_8), .in1(multiplexer_2_out), .out(multiplexer_3_out), .sel(controller_1_alubsel));  // open: en
  Multiplexer #(.select(2), .width(32)) multiplexer_4 (
    .in0(dm_1_out_8), .in1({alu_1_out_4[31:7], out_7, alu_1_out_4[1:0]}), .out(out_5),
    .sel(controller_1_grf_wdsel));  // open: in2, in3, en
  DM dm_1 (
    .in_2(clk), .in_3(in_1), .in_4({alu_1_out_4[31:7], out_7, alu_1_out_4[1:0]}), .in_5(out_8), .in_6(out_6),
    .in_7(controller_1_dm_re), .in_1(controller_1_dmoutsel), .out_8(dm_1_out_8));

  // Other names for the same wires on the sheet: MemAddr[4:0] = out_7; Instr[31:0] = out_2; MemData[31:0] = out_8;
  //   MemWrite = out_6; RegAddr[4:0] = out_4; RegData[31:0] = out_5; RegWrite = out_3; reset = in_1

  // Notes on the sheet:
  //   IFU
  //   controller
  //   Badder
  //   A3sel
  //   GRF
  //   ALU
  //   DM
endmodule

module IFU (
  input  in_1,
  input  in_2,
  input  in_3,
  input  [31:0] in_4,
  output [31:0] out_5,
  output [31:0] out_6
);

  wire [31:0] multiplexer_1_out, register_1_q;

  Multiplexer #(.width(32)) multiplexer_1 (.in0(out_6), .in1(in_4), .out(multiplexer_1_out), .sel(in_3));  // open: en
  Register #(.width(32)) register_1 (.D(multiplexer_1_out), .Q(register_1_q), .clk(in_1), .clr(in_2));  // open: en
  ROM #(.addrWidth(5), .dataWidth(32)) rom_1 (.addr(register_1_q[6:2]), .data(out_5));  // open: sel
  Adder #(.width(32)) adder_1 (.a(register_1_q), .b(32'h4), .out(out_6));  // open: cin, cout

  // Other names for the same wires on the sheet: clk = in_1; PCsel = in_3; reset = in_2

  // Notes on the sheet:
  //   Badder
  //   PC
  //   IM
  //   Adder
  //   contents of rom_1 (hex, n*v repeats v):
  //   3404007b 348501c8 3c06007b 3c07ffff 34e7ffff 868020 878820 e79020 34080000 ad040000 ad050004
  //   ad060008 ad07000c ad100010 ad110014 ad120018 8d040000 8d05000c ad04001c ad050020 34040001 34050002
  //   34060001 10850001 10860001 ad040024 ad050028 3c087777 3508ffff
  //   OP
  //   PCn
endmodule

module GRF (
  input  WE,
  input  reset,
  input  clk,
  input  [4:0] A,
  input  [4:0] A2,
  input  [4:0] A3,
  input  [31:0] in_7,
  output [31:0] out_8,
  output [31:0] out_9
);

  wire and_1_out, and_2_out, and_3_out, and_4_out, and_5_out, and_6_out, and_7_out, and_8_out, and_9_out,
       and_10_out, and_11_out, and_12_out, and_13_out, and_14_out, and_15_out, and_16_out, and_17_out,
       and_18_out, and_19_out, and_20_out, and_21_out, and_22_out, and_23_out, and_24_out, and_25_out,
       and_26_out, and_27_out, and_28_out, and_29_out, and_30_out, and_31_out, comparator_1_eq,
       comparator_2_eq, comparator_3_eq, comparator_4_eq, comparator_5_eq, comparator_6_eq, comparator_7_eq,
       comparator_8_eq, comparator_9_eq, comparator_10_eq, comparator_11_eq, comparator_12_eq,
       comparator_13_eq, comparator_14_eq, comparator_15_eq, comparator_16_eq, comparator_17_eq,
       comparator_18_eq, comparator_19_eq, comparator_20_eq, comparator_21_eq, comparator_22_eq,
       comparator_23_eq, comparator_24_eq, comparator_25_eq, comparator_26_eq, comparator_27_eq,
       comparator_28_eq, comparator_29_eq, comparator_30_eq, comparator_31_eq;
  wire [31:0] _0, _1, _2, _3, _4, _5, _6, _7, _8, _9, _10, _11, _12, _13, _14, _15, _16, _17, _18, _19, _20,
       _21, _22, _23, _24, _25, _26, _27, _28, _29, _30, _31;

  Comparator #(.width(5)) comparator_1 (.a(5'b00100), .b(A3), .eq(comparator_1_eq));  // open: gt, lt
  Comparator #(.width(5)) comparator_2 (.a(5'b01000), .b(A3), .eq(comparator_2_eq));  // open: gt, lt
  Comparator #(.width(5)) comparator_3 (.a(5'b01100), .b(A3), .eq(comparator_3_eq));  // open: gt, lt
  Comparator #(.width(5)) comparator_4 (.a(5'b10000), .b(A3), .eq(comparator_4_eq));  // open: gt, lt
  Comparator #(.width(5)) comparator_5 (.a(5'b10100), .b(A3), .eq(comparator_5_eq));  // open: gt, lt
  Comparator #(.width(5)) comparator_6 (.a(5'b11000), .b(A3), .eq(comparator_6_eq));  // open: gt, lt
  Comparator #(.width(5)) comparator_7 (.a(5'b11100), .b(A3), .eq(comparator_7_eq));  // open: gt, lt
  and and_1 (and_1_out, comparator_1_eq, WE);
  and and_2 (and_2_out, comparator_2_eq, WE);
  and and_3 (and_3_out, comparator_3_eq, WE);
  and and_4 (and_4_out, comparator_4_eq, WE);
  and and_5 (and_5_out, comparator_5_eq, WE);
  and and_6 (and_6_out, comparator_6_eq, WE);
  and and_7 (and_7_out, comparator_7_eq, WE);
  Register #(.width(32)) register_1 (.D({32{1'b0}}), .Q(_0), .clk(clk), .clr(reset));  // open: en
  Register #(.width(32)) register_2 (.D(in_7), .en(and_1_out), .Q(_4), .clk(clk), .clr(reset));
  Register #(.width(32)) register_3 (.D(in_7), .en(and_2_out), .Q(_8), .clk(clk), .clr(reset));
  Register #(.width(32)) register_4 (.D(in_7), .en(and_3_out), .Q(_12), .clk(clk), .clr(reset));
  Register #(.width(32)) register_5 (.D(in_7), .en(and_4_out), .Q(_16), .clk(clk), .clr(reset));
  Register #(.width(32)) register_6 (.D(in_7), .en(and_5_out), .Q(_20), .clk(clk), .clr(reset));
  Register #(.width(32)) register_7 (.D(in_7), .en(and_6_out), .Q(_24), .clk(clk), .clr(reset));
  Register #(.width(32)) register_8 (.D(in_7), .en(and_7_out), .Q(_28), .clk(clk), .clr(reset));
  Comparator #(.width(5)) comparator_8 (.a(5'b00001), .b(A3), .eq(comparator_8_eq));  // open: gt, lt
  Comparator #(.width(5)) comparator_9 (.a(5'b00101), .b(A3), .eq(comparator_9_eq));  // open: gt, lt
  Comparator #(.width(5)) comparator_10 (.a(5'b01001), .b(A3), .eq(comparator_10_eq));  // open: gt, lt
  Comparator #(.width(5)) comparator_11 (.a(5'b01101), .b(A3), .eq(comparator_11_eq));  // open: gt, lt
  Comparator #(.width(5)) comparator_12 (.a(5'b10001), .b(A3), .eq(comparator_12_eq));  // open: gt, lt
  Comparator #(.width(5)) comparator_13 (.a(5'b10101), .b(A3), .eq(comparator_13_eq));  // open: gt, lt
  Comparator #(.width(5)) comparator_14 (.a(5'b11001), .b(A3), .eq(comparator_14_eq));  // open: gt, lt
  Comparator #(.width(5)) comparator_15 (.a(5'b11101), .b(A3), .eq(comparator_15_eq));  // open: gt, lt
  and and_8 (and_8_out, comparator_8_eq, WE);
  and and_9 (and_9_out, comparator_9_eq, WE);
  and and_10 (and_10_out, comparator_10_eq, WE);
  and and_11 (and_11_out, comparator_11_eq, WE);
  and and_12 (and_12_out, comparator_12_eq, WE);
  and and_13 (and_13_out, comparator_13_eq, WE);
  and and_14 (and_14_out, comparator_14_eq, WE);
  and and_15 (and_15_out, comparator_15_eq, WE);
  Register #(.width(32)) register_9 (.D(in_7), .en(and_8_out), .Q(_1), .clk(clk), .clr(reset));
  Register #(.width(32)) register_10 (.D(in_7), .en(and_9_out), .Q(_5), .clk(clk), .clr(reset));
  Register #(.width(32)) register_11 (.D(in_7), .en(and_10_out), .Q(_9), .clk(clk), .clr(reset));
  Register #(.width(32)) register_12 (.D(in_7), .en(and_11_out), .Q(_13), .clk(clk), .clr(reset));
  Register #(.width(32)) register_13 (.D(in_7), .en(and_12_out), .Q(_17), .clk(clk), .clr(reset));
  Register #(.width(32)) register_14 (.D(in_7), .en(and_13_out), .Q(_21), .clk(clk), .clr(reset));
  Register #(.width(32)) register_15 (.D(in_7), .en(and_14_out), .Q(_25), .clk(clk), .clr(reset));
  Register #(.width(32)) register_16 (.D(in_7), .en(and_15_out), .Q(_29), .clk(clk), .clr(reset));
  Comparator #(.width(5)) comparator_16 (.a(5'b00010), .b(A3), .eq(comparator_16_eq));  // open: gt, lt
  Comparator #(.width(5)) comparator_17 (.a(5'b00110), .b(A3), .eq(comparator_17_eq));  // open: gt, lt
  Comparator #(.width(5)) comparator_18 (.a(5'b01010), .b(A3), .eq(comparator_18_eq));  // open: gt, lt
  Comparator #(.width(5)) comparator_19 (.a(5'b01110), .b(A3), .eq(comparator_19_eq));  // open: gt, lt
  Comparator #(.width(5)) comparator_20 (.a(5'b10010), .b(A3), .eq(comparator_20_eq));  // open: gt, lt
  Comparator #(.width(5)) comparator_21 (.a(5'b10110), .b(A3), .eq(comparator_21_eq));  // open: gt, lt
  Comparator #(.width(5)) comparator_22 (.a(5'b11010), .b(A3), .eq(comparator_22_eq));  // open: gt, lt
  Comparator #(.width(5)) comparator_23 (.a(5'b11110), .b(A3), .eq(comparator_23_eq));  // open: gt, lt
  and and_16 (and_16_out, comparator_16_eq, WE);
  and and_17 (and_17_out, comparator_17_eq, WE);
  and and_18 (and_18_out, comparator_18_eq, WE);
  and and_19 (and_19_out, comparator_19_eq, WE);
  and and_20 (and_20_out, comparator_20_eq, WE);
  and and_21 (and_21_out, comparator_21_eq, WE);
  and and_22 (and_22_out, comparator_22_eq, WE);
  and and_23 (and_23_out, comparator_23_eq, WE);
  Register #(.width(32)) register_17 (.D(in_7), .en(and_16_out), .Q(_2), .clk(clk), .clr(reset));
  Register #(.width(32)) register_18 (.D(in_7), .en(and_17_out), .Q(_6), .clk(clk), .clr(reset));
  Register #(.width(32)) register_19 (.D(in_7), .en(and_18_out), .Q(_10), .clk(clk), .clr(reset));
  Register #(.width(32)) register_20 (.D(in_7), .en(and_19_out), .Q(_14), .clk(clk), .clr(reset));
  Register #(.width(32)) register_21 (.D(in_7), .en(and_20_out), .Q(_18), .clk(clk), .clr(reset));
  Register #(.width(32)) register_22 (.D(in_7), .en(and_21_out), .Q(_22), .clk(clk), .clr(reset));
  Register #(.width(32)) register_23 (.D(in_7), .en(and_22_out), .Q(_26), .clk(clk), .clr(reset));
  Register #(.width(32)) register_24 (.D(in_7), .en(and_23_out), .Q(_30), .clk(clk), .clr(reset));
  Comparator #(.width(5)) comparator_24 (.a(5'b00011), .b(A3), .eq(comparator_24_eq));  // open: gt, lt
  Comparator #(.width(5)) comparator_25 (.a(5'b00111), .b(A3), .eq(comparator_25_eq));  // open: gt, lt
  Comparator #(.width(5)) comparator_26 (.a(5'b01011), .b(A3), .eq(comparator_26_eq));  // open: gt, lt
  Comparator #(.width(5)) comparator_27 (.a(5'b01111), .b(A3), .eq(comparator_27_eq));  // open: gt, lt
  Comparator #(.width(5)) comparator_28 (.a(5'b10011), .b(A3), .eq(comparator_28_eq));  // open: gt, lt
  Comparator #(.width(5)) comparator_29 (.a(5'b10111), .b(A3), .eq(comparator_29_eq));  // open: gt, lt
  Comparator #(.width(5)) comparator_30 (.a(5'b11011), .b(A3), .eq(comparator_30_eq));  // open: gt, lt
  Comparator #(.width(5)) comparator_31 (.a({5{1'b1}}), .b(A3), .eq(comparator_31_eq));  // open: gt, lt
  and and_24 (and_24_out, comparator_24_eq, WE);
  and and_25 (and_25_out, comparator_25_eq, WE);
  and and_26 (and_26_out, comparator_26_eq, WE);
  and and_27 (and_27_out, comparator_27_eq, WE);
  and and_28 (and_28_out, comparator_28_eq, WE);
  and and_29 (and_29_out, comparator_29_eq, WE);
  and and_30 (and_30_out, comparator_30_eq, WE);
  and and_31 (and_31_out, comparator_31_eq, WE);
  Register #(.width(32)) register_25 (.D(in_7), .en(and_24_out), .Q(_3), .clk(clk), .clr(reset));
  Register #(.width(32)) register_26 (.D(in_7), .en(and_25_out), .Q(_7), .clk(clk), .clr(reset));
  Register #(.width(32)) register_27 (.D(in_7), .en(and_26_out), .Q(_11), .clk(clk), .clr(reset));
  Register #(.width(32)) register_28 (.D(in_7), .en(and_27_out), .Q(_15), .clk(clk), .clr(reset));
  Register #(.width(32)) register_29 (.D(in_7), .en(and_28_out), .Q(_19), .clk(clk), .clr(reset));
  Register #(.width(32)) register_30 (.D(in_7), .en(and_29_out), .Q(_23), .clk(clk), .clr(reset));
  Register #(.width(32)) register_31 (.D(in_7), .en(and_30_out), .Q(_27), .clk(clk), .clr(reset));
  Register #(.width(32)) register_32 (.D(in_7), .en(and_31_out), .Q(_31), .clk(clk), .clr(reset));
  Multiplexer #(.select(5), .width(32)) multiplexer_1 (
    .in0(_0), .in1(_1), .in2(_2), .in3(_3), .in4(_4), .in5(_5), .in6(_6), .in7(_7), .in8(_8), .in9(_9),
    .in10(_10), .in11(_11), .in12(_12), .in13(_13), .in14(_14), .in15(_15), .in16(_16), .in17(_17),
    .in18(_18), .in19(_19), .in20(_20), .in21(_21), .in22(_22), .in23(_23), .in24(_24), .in25(_25),
    .in26(_26), .in27(_27), .in28(_28), .in29(_29), .in30(_30), .in31(_31), .out(out_8), .sel(A));  // open: en
  Multiplexer #(.select(5), .width(32)) multiplexer_2 (
    .in0(_0), .in1(_1), .in2(_2), .in3(_3), .in4(_4), .in5(_5), .in6(_6), .in7(_7), .in8(_8), .in9(_9),
    .in10(_10), .in11(_11), .in12(_12), .in13(_13), .in14(_14), .in15(_15), .in16(_16), .in17(_17),
    .in18(_18), .in19(_19), .in20(_20), .in21(_21), .in22(_22), .in23(_23), .in24(_24), .in25(_25),
    .in26(_26), .in27(_27), .in28(_28), .in29(_29), .in30(_30), .in31(_31), .out(out_9), .sel(A2));  // open: en

  // Other names for the same wires on the sheet: A1[4:0] = A; WD[31:0] = in_7

  // Notes on the sheet:
  //   WD
endmodule

module ALU (
  input  [31:0] in_1,
  input  [31:0] in_2,
  input  [2:0] in_3,
  output [31:0] out_4,
  output [1:0] compare
);

  wire compare_t, compareb, comparel;
  wire [1:0] multiplexer_2_out, multiplexer_3_out;
  wire [31:0] add, \or , sub;

  Adder #(.width(32)) adder_1 (.a(in_1), .b(in_2), .out(add));  // open: cin, cout
  Subtractor #(.width(32)) subtractor_1 (.a(in_1), .b(in_2), .out(sub));  // open: bin, bout
  assign \or  = in_1 | in_2;  // OR_Gate or_1, 32 bits wide
  Comparator #(.width(32), .mode("unsigned")) comparator_1 (
    .a(in_1), .b(in_2), .gt(compareb), .eq(compare_t), .lt(comparel));
  Multiplexer #(.select(3), .width(32), .disabled(0)) multiplexer_1 (
    .in0(add), .in1(sub), .in2(\or ), .in4({in_2[15:0], {16{1'b0}}}), .out(out_4), .sel(in_3));  // open: in3, in5, in6, in7, en
  Multiplexer #(.width(2)) multiplexer_2 (.in1(2'b10), .out(multiplexer_2_out), .sel(compareb));  // open: in0, en
  Multiplexer #(.width(2)) multiplexer_3 (
    .in0(multiplexer_2_out), .in1(2'b01), .out(multiplexer_3_out), .sel(comparel));  // open: en
  Multiplexer #(.width(2)) multiplexer_4 (
    .in0(multiplexer_3_out), .in1(2'b00), .out(compare), .sel(compare_t));  // open: en

  // Other names for the same wires on the sheet: data1[31:0] = in_1; data2[31:0] = in_2; lui[31:16] = in_2[15:0];
  //   op[2:0] = in_3

  // Notes on the sheet:
  //   op=011,compare
  //   op=000,add
  //   op=001,sub
  //   op=010,or
  //   op=100,lui
  //   result
endmodule

module DM (
  input  [1:0] in_1,
  input  in_2,
  input  in_3,
  input  [31:0] in_4,
  input  [31:0] in_5,
  input  in_6,
  input  in_7,
  output [31:0] out_8
);

  wire [1:0] bit_extender_1_out;
  wire [7:0] multiplexer_1_out;
  wire [31:0] \byte , word;

  Bit_Extender #(.in_width(32), .out_width(2)) bit_extender_1 (.in(in_4), .out(bit_extender_1_out));
  Multiplexer #(.select(2), .width(8)) multiplexer_1 (
    .in0(word[7:0]), .in1(word[15:8]), .in2(word[23:16]), .in3(word[31:24]), .out(multiplexer_1_out),
    .sel(bit_extender_1_out));  // open: en
  assign \byte  = {{24{multiplexer_1_out[7]}}, multiplexer_1_out};  // Bit_Extender bit_extender_2
  RAM #(.addrWidth(5), .dataWidth(32), .bus("separate")) ram_1 (
    .addr(in_4[6:2]), .din(in_5), .data(word), .str(in_6), .clk(in_2), .ld(in_7), .clr(in_3));  // open: sel
  Multiplexer #(.select(2), .width(32)) multiplexer_2 (
    .in0(word), .in1(\byte ), .out(out_8), .sel(in_1));  // open: in2, in3, en

  // Other names for the same wires on the sheet: address[31:0] = in_4; clk = in_2; DMoutsel[1:0] = in_1; RE = in_7;
  //   reset = in_3; WD[31:0] = in_5; WE = in_6

  // Notes on the sheet:
  //   Output
endmodule

module Badder (
  input  [2:0] ad1,
  input  [31:0] in_2,
  input  [31:0] in_3,
  input  [1:0] compare,
  input  [31:0] in_5,
  output [31:0] out_6
);

  wire equ;
  wire [27:0] PC;
  wire [31:0] beq, multiplexer_1_out, offset;
  wire [31:28] j;

  Subtractor #(.width(32)) subtractor_1 (.a(in_2), .b(32'h4), .out({j, PC}));  // open: bin, bout
  Shifter #(.width(32)) shifter_1 (.in(in_3), .\dist (5'b00010), .out(offset));
  Comparator #(.width(2), .mode("unsigned")) comparator_1 (.a(compare), .b(2'b00), .eq(equ));  // open: gt, lt
  Multiplexer #(.width(32)) multiplexer_1 (
    .in0({32{1'b0}}), .in1(offset), .out(multiplexer_1_out), .sel(equ));  // open: en
  Adder #(.width(32)) adder_1 (.a(in_2), .b(multiplexer_1_out), .out(beq));  // open: cin, cout
  Multiplexer #(.select(3), .width(32)) multiplexer_2 (
    .in0(in_2), .in1(beq), .in2({j, in_5[25:0], 2'b00}), .out(out_6), .sel(ad1));  // open: in3, in4, in5, in6, in7, en

  // Other names for the same wires on the sheet: Basel[2:0] = ad1; com[1:0] = compare; j[27:2] = in_5[25:0];
  //   OP[31:0] = in_5; PC[31:28] = j; PC_4[31:0] = in_2

  // Notes on the sheet:
  //   ad2
  //   Baout
endmodule

module Controller (
  input  [5:0] op,
  input  [5:0] func,
  output PCsel,
  output GRF_WE,
  output DM_WE,
  output DM_RE,
  output ALUBsel,
  output signextsel,
  output [2:0] Basel,
  output [2:0] ALU_OP,
  output [1:0] GRF_A3sel,
  output [1:0] GRF_WDsel,
  output [1:0] DMoutsel
);

  wire add, lw, not_1_out, not_2_out, not_3_out, not_4_out, not_5_out, not_6_out, not_7_out, not_8_out,
       not_9_out, not_10_out, not_11_out, not_12_out, sub;

  not not_1 (not_1_out, op[4]);
  not not_2 (not_2_out, op[5]);
  not not_3 (not_3_out, op[2]);
  not not_4 (not_4_out, op[3]);
  not not_5 (not_5_out, op[1]);
  not not_6 (not_6_out, op[0]);
  not not_7 (not_7_out, func[4]);
  not not_8 (not_8_out, func[5]);
  not not_9 (not_9_out, func[2]);
  not not_10 (not_10_out, func[3]);
  not not_11 (not_11_out, func[0]);
  not not_12 (not_12_out, func[1]);
  and and_1 (add, not_2_out, not_1_out, not_4_out, not_3_out, not_5_out, not_6_out, func[5], not_7_out, not_10_out, not_9_out, not_12_out, not_11_out);
  and and_2 (sub, not_2_out, not_1_out, not_4_out, not_3_out, not_5_out, not_6_out, func[5], not_7_out, not_10_out, not_9_out, func[1], not_11_out);
  and and_3 (signextsel, not_2_out, not_1_out, op[3], op[2], not_5_out, op[0]);
  and and_4 (lw, op[5], not_1_out, not_4_out, not_3_out, op[1], op[0]);
  and and_5 (DM_WE, op[5], not_1_out, op[3], not_3_out, op[1], op[0]);
  and and_6 (ALU_OP[2], not_2_out, not_1_out, op[3], op[2], op[1], op[0]);
  and and_7 (Basel[0], not_2_out, not_1_out, not_4_out, op[2], not_5_out, not_6_out);
  and and_8 (DMoutsel[0], op[5], not_1_out, not_4_out, not_3_out, not_5_out, not_6_out);
  and and_9 (Basel[1], not_2_out, not_1_out, not_4_out, not_3_out, op[1], not_6_out);
  or or_1 (PCsel, Basel[1], Basel[0]);
  or or_2 (GRF_WE, signextsel, add, sub, lw, ALU_OP[2], DMoutsel[0]);
  or or_3 (ALU_OP[1], signextsel, Basel[0]);
  or or_4 (ALU_OP[0], sub, Basel[0]);
  or or_5 (DM_RE, lw, DMoutsel[0]);
  or or_6 (GRF_A3sel[0], add, sub);
  or or_7 (ALUBsel, signextsel, lw, DMoutsel[0], DM_WE, ALU_OP[2]);
  or or_8 (GRF_WDsel[0], add, sub, signextsel, ALU_OP[2]);

  assign Basel[2] = 1'b0;
  assign DMoutsel[1] = 1'b0;
  assign GRF_A3sel[1] = 1'b0;
  assign GRF_WDsel[1] = 1'b0;

  // Other names for the same wires on the sheet: lui = ALU_OP[2]; beq = Basel[0]; j = Basel[1]; lb = DMoutsel[0];
  //   ori = signextsel; sw = DM_WE
endmodule
